// Logisim project TriggerT.circ as structural Verilog: 1 circuit, main circuit main
module main (
  input  S,
  input  in_2,
  input  x1,
  input  S_2,
  input  x2,
  input  in_6,
  input  R,
  input  x3,
  input  in_9,
  input  R_2,
  input  x4,
  input  in_12,
  input  S_3,
  input  in_14,
  input  in_15,
  input  in_16,
  input  R_3,
  output nQ,
  output out_19,
  output out_20,
  output out_21,
  output nQ_2,
  output Q,
  output Q_2,
  output nQ_3,
  output out_26,
  output Q_3,
  output out_28,
  output [3:0] out_29,
  output Q_4,
  output nQ_4
);

  wire and_1_out, and_2_out, and_3_out, and_4_out, and_5_out, and_6_out, and_7_out, and_8_out, and_9_out,
       and_10_out, and_11_out, and_12_out, and_13_out, and_14_out, nand_1_out, nand_2_out, nand_7_out,
       nand_8_out, nand_9_out, nand_10_out, nand_11_out, nand_12_out, nand_13_out, nand_14_out, nand_15_out,
       nand_16_out, nand_17_out, nand_18_out, nand_19_out, nand_20_out, nand_21_out, nand_22_out,
       nand_23_out, nand_24_out, nand_26_out, nand_28_out, nand_30_out, nand_31_out, nand_32_out,
       nand_33_out, nand_34_out, nand_35_out, nand_36_out, nand_38_out, not_3_out, not_4_out, not_5_out,
       not_6_out;

  not not_1 (out_19, in_2);
  not not_2 (in_2, out_19);
  nand nand_1 (nand_1_out, nQ_4, S_3, in_15);
  nand nand_2 (nand_2_out, in_15, R_3, Q_4);
  nand nand_3 (Q_4, nand_1_out, nQ_4);
  nand nand_4 (nQ_4, Q_4, nand_2_out);
  nand nand_5 (nQ, S, Q);
  nor nor_1 (nQ_3, in_9, Q_3);
  nand nand_6 (Q, nQ, R);
  nor nor_2 (Q_3, nQ_3, in_12);
  nand nand_7 (nand_7_out, nand_26_out, in_14, in_16);
  nand nand_8 (nand_8_out, in_16, in_14, out_29[0]);
  nand nand_9 (nand_9_out, nand_28_out, out_29[0], in_16);
  nand nand_10 (nand_10_out, in_16, out_29[0], out_29[1]);
  nand nand_11 (nand_11_out, nand_30_out, and_3_out, in_16);
  nand nand_12 (nand_12_out, in_16, and_3_out, out_29[2]);
  nand nand_13 (nand_13_out, nand_7_out, nand_14_out);
  nand nand_14 (nand_14_out, nand_13_out, nand_8_out);
  nand nand_15 (nand_15_out, nand_9_out, nand_16_out);
  nand nand_16 (nand_16_out, nand_15_out, nand_10_out);
  nand nand_17 (nand_17_out, nand_11_out, nand_18_out);
  nand nand_18 (nand_18_out, nand_17_out, nand_12_out);
  nand nand_19 (nand_19_out, nand_7_out, nand_13_out);
  nand nand_20 (nand_20_out, nand_14_out, nand_8_out);
  nand nand_21 (nand_21_out, nand_9_out, nand_15_out);
  nand nand_22 (nand_22_out, nand_16_out, nand_10_out);
  nand nand_23 (nand_23_out, nand_11_out, nand_17_out);
  nand nand_24 (nand_24_out, nand_18_out, nand_12_out);
  and and_1 (and_1_out, S_2, in_6);
  and and_2 (and_2_out, in_6, R_2);
  nand nand_25 (out_29[0], nand_19_out, nand_26_out);
  nand nand_26 (nand_26_out, out_29[0], nand_20_out);
  nand nand_27 (out_29[1], nand_21_out, nand_28_out);
  nand nand_28 (nand_28_out, out_29[1], nand_22_out);
  nand nand_29 (out_29[2], nand_23_out, nand_30_out);
  nand nand_30 (nand_30_out, out_29[2], nand_24_out);
  nor nor_3 (nQ_2, and_1_out, Q_2);
  nor nor_4 (Q_2, nQ_2, and_2_out);
  and and_3 (and_3_out, out_29[0], out_29[1]);
  and and_4 (and_4_out, out_29[0], out_29[1], out_29[2]);
  nand nand_31 (nand_31_out, nand_38_out, and_4_out, in_16);
  nand nand_32 (nand_32_out, in_16, and_4_out, out_29[3]);
  nand nand_33 (nand_33_out, nand_31_out, nand_34_out);
  nand nand_34 (nand_34_out, nand_33_out, nand_32_out);
  nand nand_35 (nand_35_out, nand_31_out, nand_33_out);
  nand nand_36 (nand_36_out, nand_34_out, nand_32_out);
  nand nand_37 (out_29[3], nand_35_out, nand_38_out);
  nand nand_38 (nand_38_out, out_29[3], nand_36_out);
  not not_3 (not_3_out, x1);
  not not_4 (not_4_out, x2);
  not not_5 (not_5_out, x3);
  not not_6 (not_6_out, x4);
  and and_5 (and_5_out, x1, not_5_out);
  and and_6 (and_6_out, x1, x3, not_6_out);
  and and_7 (and_7_out, x1, not_4_out);
  and and_8 (and_8_out, not_3_out, x2, x3, x4);
  and and_9 (and_9_out, x2, not_5_out);
  and and_10 (and_10_out, x2, x3, not_6_out);
  and and_11 (and_11_out, not_3_out, not_4_out, x3, x4);
  and and_12 (and_12_out, x1, not_4_out, x3, x4);
  and and_13 (and_13_out, not_5_out, x4);
  and and_14 (and_14_out, x3, not_6_out);
  or or_1 (out_20, and_5_out, and_6_out, and_7_out, and_8_out);
  or or_2 (out_26, and_9_out, and_10_out, and_11_out, and_12_out);
  or or_3 (out_28, and_13_out, and_14_out);

  assign out_21 = in_2;

  // Notes on the sheet:
  //   Бит синхронизации
  //   Простой flip-flop
  //   Синхронный JK-триггер
  //   RS-триггер
  //   Многоуровневый Синхронный JK-триггер
  //   Бит синхронизации
  //   Синхронный RS-триггер
  //   !x1
  //   !x2
  //   !x3
  //   !x4
  //   x1
  //   x2
  //   x3
  //   x4
  //   !x1
  //   !x2
  //   !x3
  //   !x4
endmodule
